# Fritzing sketch Sensing Circuit Slip and Trip (saved by Fritzing 0.9.10b)
circuit board: 13cm x 15cm
breadboards: 1

parts:
  part = Arduino Uno (Rev3)
  SparkFun_Breakout_ADC = Analog Digital MUX Breakout
  SparkFun_Breakout_ADC_2 = Analog Digital MUX Breakout
  R7 = Resistor [tolerance=±5% resistance=1M package="0805 [SMD]"]
  R8 = Resistor [tolerance=±5% resistance=1M package="0805 [SMD]"]
  R11 = Resistor [tolerance=±5% resistance=1M package="0805 [SMD]"]
  R1 = Resistor [tolerance=±5% resistance=1M package="0805 [SMD]"]
  R0-15 = Resistor [tolerance=±5% resistance=1M package="0805 [SMD]"]
  R9 = Resistor [tolerance=±5% resistance=1M package="0805 [SMD]"]
  R2 = Resistor [tolerance=±5% resistance=1M package="0805 [SMD]"]
  R10 = Resistor [tolerance=±5% resistance=1M package="0805 [SMD]"]
  R5 = Resistor [tolerance=±5% resistance=1M package="0805 [SMD]"]
  R4 = Resistor [tolerance=±5% resistance=1M package="0805 [SMD]"]
  R3 = Resistor [tolerance=±5% resistance=1M package="0805 [SMD]"]
  R5_2 = Resistor [tolerance=±5% resistance=1M package="0805 [SMD]"]
  Too_Copper_Rows_(FEMALE_HEADER_PINS) = female pin header, 16 pins [form="♀ (female)"]
  Too_Copper_Columns_(FEMALE_HEADER_PINS) = female pin header, 16 pins [form="♀ (female)"]
  R12 = Resistor [tolerance=±5% resistance=1M package="0805 [SMD]"]
  R-13 = Resistor [tolerance=±5% resistance=1M package="0805 [SMD]"]
  R-15 = Resistor [tolerance=±5% resistance=1M package="0805 [SMD]"]
  R-16 = Resistor [tolerance=±5% resistance=1M package="0805 [SMD]"]

nets:
  N1: part.A0, SparkFun_Breakout_ADC_2.SIG
  N2: part.A1, SparkFun_Breakout_ADC_2.S3
  N3: part.A2, SparkFun_Breakout_ADC_2.S2
  N4: part.A3, SparkFun_Breakout_ADC_2.S1
  N5: part.A4/SDA, SparkFun_Breakout_ADC_2.S0
  GND: part.GND, SparkFun_Breakout_ADC.GND, SparkFun_Breakout_ADC.EN, SparkFun_Breakout_ADC_2.GND, SparkFun_Breakout_ADC_2.EN, R7.Pin_0, R8.Pin_0, R11.Pin_0, R1.Pin_0, R0-15.Pin_0, R9.Pin_0, R2.Pin_0, R10.Pin_0, R5.Pin_0, R4.Pin_0, R3.Pin_0, R5_2.Pin_0, R12.Pin_0, R-13.Pin_0, R-15.Pin_0, R-16.Pin_0
  N6: part.D2, SparkFun_Breakout_ADC.SIG
  N7: part.D3_PWM, SparkFun_Breakout_ADC.S3
  N8: part.D4, SparkFun_Breakout_ADC.S2
  N9: part.D5_PWM, SparkFun_Breakout_ADC.S1
  N10: part.D6_PWM, SparkFun_Breakout_ADC.S0
  VCC: part.5V, SparkFun_Breakout_ADC.VCC, SparkFun_Breakout_ADC_2.VCC
  N11: SparkFun_Breakout_ADC.C0, Too_Copper_Rows_(FEMALE_HEADER_PINS).pin16
  N12: SparkFun_Breakout_ADC.C1, Too_Copper_Rows_(FEMALE_HEADER_PINS).pin15
  N13: SparkFun_Breakout_ADC.C2, Too_Copper_Rows_(FEMALE_HEADER_PINS).pin14
  N14: SparkFun_Breakout_ADC.C3, Too_Copper_Rows_(FEMALE_HEADER_PINS).pin13
  N15: SparkFun_Breakout_ADC.C4, Too_Copper_Rows_(FEMALE_HEADER_PINS).pin12
  N16: SparkFun_Breakout_ADC.C5, Too_Copper_Rows_(FEMALE_HEADER_PINS).pin11
  N17: SparkFun_Breakout_ADC.C6, Too_Copper_Rows_(FEMALE_HEADER_PINS).pin10
  N18: SparkFun_Breakout_ADC.C7, Too_Copper_Rows_(FEMALE_HEADER_PINS).pin9
  N19: SparkFun_Breakout_ADC.C8, Too_Copper_Rows_(FEMALE_HEADER_PINS).pin8
  N20: SparkFun_Breakout_ADC.C9, Too_Copper_Rows_(FEMALE_HEADER_PINS).pin7
  N21: SparkFun_Breakout_ADC.C10, Too_Copper_Rows_(FEMALE_HEADER_PINS).pin6
  N22: SparkFun_Breakout_ADC.C11, Too_Copper_Rows_(FEMALE_HEADER_PINS).pin5
  N23: SparkFun_Breakout_ADC.C12, Too_Copper_Rows_(FEMALE_HEADER_PINS).pin4
  N24: SparkFun_Breakout_ADC.C13, Too_Copper_Rows_(FEMALE_HEADER_PINS).pin3
  N25: SparkFun_Breakout_ADC.C14, Too_Copper_Rows_(FEMALE_HEADER_PINS).pin2
  N26: SparkFun_Breakout_ADC.C15, Too_Copper_Rows_(FEMALE_HEADER_PINS).pin1
  N27: SparkFun_Breakout_ADC_2.C0, R1.Pin_1, Too_Copper_Columns_(FEMALE_HEADER_PINS).pin1
  N28: SparkFun_Breakout_ADC_2.C1, R2.Pin_1, Too_Copper_Columns_(FEMALE_HEADER_PINS).pin2
  N29: SparkFun_Breakout_ADC_2.C2, R3.Pin_1, Too_Copper_Columns_(FEMALE_HEADER_PINS).pin3
  N30: SparkFun_Breakout_ADC_2.C3, R4.Pin_1, Too_Copper_Columns_(FEMALE_HEADER_PINS).pin4
  N31: SparkFun_Breakout_ADC_2.C4, R5_2.Pin_1, Too_Copper_Columns_(FEMALE_HEADER_PINS).pin5
  N32: SparkFun_Breakout_ADC_2.C5, R5.Pin_1, Too_Copper_Columns_(FEMALE_HEADER_PINS).pin6
  N33: SparkFun_Breakout_ADC_2.C6, R7.Pin_1, Too_Copper_Columns_(FEMALE_HEADER_PINS).pin7
  N34: SparkFun_Breakout_ADC_2.C7, R8.Pin_1, Too_Copper_Columns_(FEMALE_HEADER_PINS).pin8
  N35: SparkFun_Breakout_ADC_2.C8, R9.Pin_1, Too_Copper_Columns_(FEMALE_HEADER_PINS).pin9
  N36: SparkFun_Breakout_ADC_2.C9, R10.Pin_1, Too_Copper_Columns_(FEMALE_HEADER_PINS).pin10
  N37: SparkFun_Breakout_ADC_2.C10, R11.Pin_1, Too_Copper_Columns_(FEMALE_HEADER_PINS).pin11
  N38: SparkFun_Breakout_ADC_2.C11, Too_Copper_Columns_(FEMALE_HEADER_PINS).pin12, R12.Pin_1
  N39: SparkFun_Breakout_ADC_2.C12, Too_Copper_Columns_(FEMALE_HEADER_PINS).pin13, R-13.Pin_1
  N40: SparkFun_Breakout_ADC_2.C13, R0-15.Pin_1, Too_Copper_Columns_(FEMALE_HEADER_PINS).pin14
  N41: SparkFun_Breakout_ADC_2.C14, Too_Copper_Columns_(FEMALE_HEADER_PINS).pin15, R-15.Pin_1
  N42: SparkFun_Breakout_ADC_2.C15, Too_Copper_Columns_(FEMALE_HEADER_PINS).pin16, R-16.Pin_1

// code stored in the sketch: Fritzing Sensing Circuit Code.ino
//Mux control pins for analog signal (SIG_pin) default for arduino mini pro
const byte s0 = A4;
const byte s1 = A3;
const byte s2 = A2;
const byte s3 = A1;

//Mux control pins for Output signal (OUT_pin) default for arduino mini pro
const byte w0 = 6; 
const byte w1 = 5;
const byte w2 = 4;
const byte w3 = 3;

//Mux in "SIG" pin default for arduino mini pro 
const byte SIG_pin = A0; 

//Mux out "SIG" pin default for arduino mini pro
const byte OUT_pin = 2;

//Row and Column pins default for arduino mini pro
//const byte STATUS_pin = 8;
//const byte COL_pin = 9;

const boolean muxChannel[16][4]={
    {0,0,0,0}, //channel 0
    {1,0,0,0}, //channel 1
    {0,1,0,0}, //channel 2
    {1,1,0,0}, //channel 3
    {0,0,1,0}, //channel 4
    {1,0,1,0}, //channel 5
    {0,1,1,0}, //channel 6
    {1,1,1,0}, //channel 7
    {0,0,0,1}, //channel 8
    {1,0,0,1}, //channel 9
    {0,1,0,1}, //channel 10
    {1,1,0,1}, //channel 11
    {0,0,1,1}, //channel 12
    {1,0,1,1}, //channel 13
    {0,1,1,1}, //channel 14
    {1,1,1,1}  //channel 15
  };


//incoming serial byte
int inByte = 0;

int valor = 0;               //variable for sending bytes to processing
int calibra[15][15];         //Calibration array for the min values of each od the 225 sensors.
int minsensor=254;          //Variable for staring the min array
int multiplier = 254;
int pastmatrix[15][15];

void setup(){
    
  pinMode(s0, OUTPUT); 
  pinMode(s1, OUTPUT); 
  pinMode(s2, OUTPUT); 
  pinMode(s3, OUTPUT); 
  
  pinMode(w0, OUTPUT); 
  pinMode(w1, OUTPUT); 
  pinMode(w2, OUTPUT); 
  pinMode(w3, OUTPUT); 
  
  pinMode(OUT_pin, OUTPUT); 
  
 // pinMode(STATUS_pin, OUTPUT);
  //pinMode(COL_pin, OUTPUT);

  
  digitalWrite(s0, LOW);
  digitalWrite(s1, LOW);
  digitalWrite(s2, LOW);
  digitalWrite(s3, LOW);
  
  digitalWrite(w0, LOW);
  digitalWrite(w1, LOW);
  digitalWrite(w2, LOW);
  digitalWrite(w3, LOW);
  
  digitalWrite(OUT_pin, HIGH);
//  digitalWrite(STATUS_pin, HIGH);
//  digitalWrite(COL_pin, HIGH);
  
 
  
  Serial.begin(115200);
  
  Serial.println("\n\Calibrating...\n");
  
  // Full of 0's of initial matrix
  for(byte j = 0; j < 15; j ++){ 
    writeMux(j);
    for(byte i = 0; i < 15; i ++)
      calibra[j][i] = 0;
  }
  
  // Calibration
  for(byte k = 0; k < 50; k++){  
    for(byte j = 0; j < 15; j ++){ 
      writeMux(j);
      for(byte i = 0; i < 15; i ++)
        calibra[j][i] = calibra[j][i] + readMux(i);
    }
  }
  
  //Print averages
  for(byte j = 0; j < 15; j ++){ 
    writeMux(j);
    for(byte i = 0; i < 15; i ++){
      calibra[j][i] = calibra[j][i]/50;
      if(calibra[j][i] < minsensor)
        minsensor = calibra[j][i];
      Serial.print(calibra[j][i]);
      Serial.print("\t");
    }
  Serial.println(); 
  }
  
  Serial.println();
  Serial.print("Minimum Value: ");
  Serial.println(minsensor);
  Serial.println();
  
  establishContact();
 
  //digitalWrite(COL_pin, LOW);
}


void loop(){
  //Loop through and read all 16 values
  //Reports back Value at channel 6 is: 346
  if (Serial.available() > 0){
    inByte = Serial.read();
    
    if(inByte == 'A'){
    
      for(int j = 14; j >= 0; j--){ 
        writeMux(j);
        
        for(int i = 0; i < 15; i++){
            
          valor = readMux(i);
          
          //Saturation sensors
          int limsup = 450;
          if(valor > limsup)
            valor = limsup;
            
          if(valor < calibra[j][i])
            valor = calibra[j][i];  
          
          valor = map(valor,minsensor, limsup,1,254); 
          
          if(valor < 150)
            valor = 0;
          if(valor > 254)
            valor = 254;

      	 //Serial.print("\t");  // For Debugging in serial terminal only
         //Serial.print(valor);
          
          Serial.write(valor);
//          digitalWrite(COL_pin,!digitalRead(COL_pin));
        } 
				//	Serial.println(); // Breaking between lines of debug output 
      }
				//  Serial.println("New Reading")
    }
        
  }
}


int readMux(byte channel){
  byte controlPin[] = {s0, s1, s2, s3};

  //loop through the 4 sig
  for(int i = 0; i < 4; i ++){
    digitalWrite(controlPin[i], muxChannel[channel][i]);
  }

  //read the value at the SIG pin
  int val = analogRead(SIG_pin);

  //return the value
  return val;
}

void writeMux(byte channel){
  byte controlPin[] = {w0, w1, w2, w3};

  //loop through the 4 sig
  for(byte i = 0; i < 4; i ++){
    digitalWrite(controlPin[i], muxChannel[channel][i]);
  }
}

void establishContact() {
  while (Serial.available() <= 0) {
    Serial.print('A');   // send a capital A
    delay(300);
  }
}
